# Fritzing sketch TMP007 (saved by Fritzing 0.9.3b)
circuit board: 4.41457cm x 4.44047cm
breadboards: 1

parts:
  Part1 = TMP007
  JP1 = Header 5x2 [package=2x5-ra]

nets:
  N1: Part1.connector4, JP1.1
  N2: Part1.connector5, JP1.9
  N3: Part1.connector6, JP1.3
  N4: Part1.connector7, JP1.5
